// Logisim project HW4FIN.circ as structural Verilog: 7 circuits, main circuit main
module main (
  input  in_1,
  output [15:0] out_2,
  output [2:0] out_3,
  output [2:0] out_4,
  output [2:0] out_5,
  output [5:0] out_6,
  output [15:0] out_7
);

  wire alu_1_ble_bne_out, and_1_out, and_2_out, button_1_out, clock_1_out, halt_out, new_new_con_1_alusrc,
       new_new_con_1_branch, new_new_con_1_call, new_new_con_1_halt, new_new_con_1_jump,
       new_new_con_1_memread, new_new_con_1_memtoreg, new_new_con_1_memwrite, new_new_con_1_regdst,
       new_new_con_1_regwrite, new_new_con_1_rtn;
  wire [2:0] new_new_con_1_aluop0;
  wire [15:0] adder_1_out, adder_2_out, adder_3_out, alu_1_alu_output, bit_extender_1_out, multiplexer_1_out,
       multiplexer_3_out, multiplexer_4_out, multiplexer_5_out, multiplexer_6_out, PC_q, ram_1_data,
       register_1_q, register_file_1_data_1, register_file_1_data_2;

  ROM #(.addrWidth(16), .dataWidth(16)) rom_1 ();  // open: addr, data, sel
  Register #(.width(16)) PC (.D(multiplexer_5_out), .en(in_1), .Q(PC_q), .clk(and_1_out), .clr(button_1_out));
  Button button_1 (.out(button_1_out));
  Clock clock_1 (.out(clock_1_out));
  and and_1 (and_1_out, clock_1_out, halt_out);
  not halt (halt_out, new_new_con_1_halt);
  ROM #(.addrWidth(16), .dataWidth(16)) rom_2 ();  // open: addr, data, sel
  Adder #(.width(16)) adder_1 (.a(16'h1), .b(PC_q), .out(adder_1_out));  // open: cin, cout
  ROM #(.addrWidth(16), .dataWidth(16)) rom_3 (.addr(PC_q), .data(out_2), .sel(1'b1));
  ROM #(.addrWidth(16), .dataWidth(16)) rom_4 ();  // open: addr, data, sel
  assign bit_extender_1_out = {{4{1'b0}}, out_2[15:4]};  // Bit_Extender bit_extender_1
  ROM #(.addrWidth(16), .dataWidth(16)) rom_5 ();  // open: addr, data, sel
  new_new_Con new_new_con_1 (
    .opocode3(out_2[3]), .opcode2(out_2[2]), .RegDst(new_new_con_1_regdst), .opcode1(out_2[1]),
    .opcode0(out_2[0]), .RegWrite(new_new_con_1_regwrite), .ALUSrc(new_new_con_1_alusrc),
    .ALUOp2(new_new_con_1_aluop0[2]), .ALUOp1(new_new_con_1_aluop0[1]), .ALUOp0(new_new_con_1_aluop0[0]),
    .MemRead(new_new_con_1_memread), .MemWrite(new_new_con_1_memwrite), .MemToReg(new_new_con_1_memtoreg),
    .Branch(new_new_con_1_branch), .Jump(new_new_con_1_jump), .Halt(new_new_con_1_halt),
    .Call(new_new_con_1_call), .rtn(new_new_con_1_rtn));
  assign out_7 = {{10{out_2[15]}}, {out_2[15], out_2[8:4]}};  // Bit_Extender bit_extender_2
  Register #(.width(16)) register_1 (
    .D(adder_1_out), .en(new_new_con_1_call), .Q(register_1_q), .clk(and_1_out));  // open: clr
  ROM #(.addrWidth(16), .dataWidth(16)) rom_6 ();  // open: addr, data, sel
  Adder #(.width(16)) adder_2 (.a(PC_q), .b(out_7), .out(adder_2_out));  // open: cin, cout
  and and_2 (and_2_out, alu_1_ble_bne_out, new_new_con_1_branch);
  Multiplexer #(.width(16), .enable("false")) multiplexer_1 (
    .in0(adder_1_out), .in1(adder_2_out), .out(multiplexer_1_out), .sel(and_2_out));
  Adder #(.width(16)) adder_3 (.a(PC_q), .b(bit_extender_1_out), .out(adder_3_out));  // open: cin, cout
  Register_File register_file_1 (
    .write_enable(new_new_con_1_regwrite), .write_reg_position(out_3), .data_Input(multiplexer_6_out),
    .clock(and_1_out), .data_1(register_file_1_data_1), .data_2(register_file_1_data_2),
    .read_reg1(out_2[11:9]), .read_reg2(out_2[14:12]));  // open: reset
  Multiplexer #(.width(3), .enable("false")) multiplexer_2 (
    .in0(out_2[14:12]), .in1(out_2[8:6]), .out(out_3), .sel(new_new_con_1_regdst));
  Multiplexer #(.width(16), .enable("false")) multiplexer_3 (
    .in0(multiplexer_1_out), .in1(adder_3_out), .out(multiplexer_3_out), .sel(new_new_con_1_jump));
  Multiplexer #(.width(16), .enable("false")) multiplexer_4 (
    .in0(register_file_1_data_2), .in1(out_7), .out(multiplexer_4_out), .sel(new_new_con_1_alusrc));
  Multiplexer #(.width(16), .enable("false")) multiplexer_5 (
    .in0(multiplexer_3_out), .in1(register_1_q), .out(multiplexer_5_out), .sel(new_new_con_1_rtn));
  ALU alu_1 (
    .Data_1(register_file_1_data_1), .Data_2(multiplexer_4_out), .ALU_OUTPUT(alu_1_alu_output),
    .ALU_Select(new_new_con_1_aluop0), .ble_bne_out(alu_1_ble_bne_out));  // open: Equal, LE, ble_equ_or_les, bne_not_equ
  RAM #(.addrWidth(16), .dataWidth(16), .bus("separate")) ram_1 (
    .addr(alu_1_alu_output), .din(register_file_1_data_2), .data(ram_1_data), .str(new_new_con_1_memwrite),
    .clk(and_1_out), .ld(new_new_con_1_memread));  // open: sel, clr
  Multiplexer #(.width(16), .enable("false")) multiplexer_6 (
    .in0(alu_1_alu_output), .in1(ram_1_data), .out(multiplexer_6_out), .sel(new_new_con_1_memtoreg));

  assign out_4 = out_2[11:9];
  assign out_5 = out_2[14:12];
  assign out_6 = {out_2[15], out_2[8:4]};

  // Notes on the sheet:
  //   Test Sam1
  //   contents of rom_1 (hex, n*v repeats v):
  //   0 1010 2020 30a0 2281 b5fa f
  //   Test Sam2
  //   contents of rom_2 (hex, n*v repeats v):
  //   0 1060 2050 1638 3889 f
  //   Test Sam3
  //   contents of rom_3 (hex, n*v repeats v):
  //   0 1020 2217 f
  //   contents of rom_4 (hex, n*v repeats v):
  //   0 1060 2050 22c2 7000 76b5 2303 7010 78c5 7010 7ce4 f
  //   Test Sam4
  //   contents of rom_5 (hex, n*v repeats v):
  //   0 1060 2040 7d 4606 1070 2080 3d 5606 3c 22c1 e f
  //   Test Sam5
  //   contents of rom_6 (hex, n*v repeats v):
  //   0 1020 2217 f
endmodule

module Register_File (
  input  write_enable,
  input  [2:0] read_reg1,
  input  [2:0] read_reg2,
  input  [2:0] write_reg_position,
  input  [15:0] data_Input,
  input  clock,
  input  reset,
  output [15:0] data_1,
  output [15:0] data_2
);

  wire and_1_out, and_2_out, and_3_out, and_4_out, and_5_out, and_6_out, and_7_out, and_8_out,
       decoder_1_out0, decoder_1_out1, decoder_1_out2, decoder_1_out3, decoder_1_out4, decoder_1_out5,
       decoder_1_out6, decoder_1_out7;
  wire [15:0] register_1_q, register_2_q, register_3_q, register_4_q, register_5_q, register_6_q,
       register_7_q, register_8_q;

  Decoder #(.select(3), .enable("false")) decoder_1 (
    .out0(decoder_1_out0), .out1(decoder_1_out1), .out2(decoder_1_out2), .out3(decoder_1_out3),
    .out4(decoder_1_out4), .out5(decoder_1_out5), .out6(decoder_1_out6), .out7(decoder_1_out7),
    .sel(write_reg_position));
  and and_1 (and_1_out, decoder_1_out0, write_enable);
  and and_2 (and_2_out, decoder_1_out1, write_enable);
  and and_3 (and_3_out, decoder_1_out2, write_enable);
  and and_4 (and_4_out, decoder_1_out3, write_enable);
  and and_5 (and_5_out, decoder_1_out4, write_enable);
  and and_6 (and_6_out, decoder_1_out5, write_enable);
  and and_7 (and_7_out, decoder_1_out6, write_enable);
  and and_8 (and_8_out, decoder_1_out7, write_enable);
  Register #(.width(16)) register_1 (.D(data_Input), .en(and_1_out), .Q(register_1_q), .clk(clock), .clr(reset));
  Register #(.width(16)) register_2 (.D(data_Input), .en(and_2_out), .Q(register_2_q), .clk(clock), .clr(reset));
  Register #(.width(16)) register_3 (.D(data_Input), .en(and_3_out), .Q(register_3_q), .clk(clock), .clr(reset));
  Register #(.width(16)) register_4 (.D(data_Input), .en(and_4_out), .Q(register_4_q), .clk(clock), .clr(reset));
  Register #(.width(16)) register_5 (.D(data_Input), .en(and_5_out), .Q(register_5_q), .clk(clock), .clr(reset));
  Register #(.width(16)) register_6 (.D(data_Input), .en(and_6_out), .Q(register_6_q), .clk(clock), .clr(reset));
  Register #(.width(16)) register_7 (.D(data_Input), .en(and_7_out), .Q(register_7_q), .clk(clock), .clr(reset));
  Register #(.width(16)) register_8 (.D(data_Input), .en(and_8_out), .Q(register_8_q), .clk(clock), .clr(reset));
  Multiplexer #(.select(3), .width(16), .enable("false")) multiplexer_1 (
    .in0(register_1_q), .in1(register_2_q), .in2(register_3_q), .in3(register_4_q), .in4(register_5_q),
    .in5(register_6_q), .in6(register_7_q), .in7(register_8_q), .out(data_1), .sel(read_reg1));
  Multiplexer #(.select(3), .width(16), .enable("false")) multiplexer_2 (
    .in0(register_1_q), .in1(register_2_q), .in2(register_3_q), .in3(register_4_q), .in4(register_5_q),
    .in5(register_6_q), .in6(register_7_q), .in7(register_8_q), .out(data_2), .sel(read_reg2));
endmodule

module ALU (
  input  [15:0] Data_1,
  input  [15:0] Data_2,
  input  [2:0] ALU_Select,
  output [15:0] ALU_OUTPUT,
  output Equal,
  output ble_equ_or_les,
  output LE,
  output ble_bne_out,
  output bne_not_equ
);

  wire [15:0] adder_1_out, and_1_out, or_1_out, subtractor_1_out;

  Adder #(.width(16)) adder_1 (.a(Data_1), .b(Data_2), .out(adder_1_out));  // open: cin, cout
  Subtractor #(.width(16)) subtractor_1 (.a(Data_1), .b(Data_2), .out(subtractor_1_out));  // open: bin, bout
  assign and_1_out = Data_1 & Data_2;  // AND_Gate and_1, 16 bits wide
  assign or_1_out = Data_1 | Data_2;  // OR_Gate or_1, 16 bits wide
  Comparator #(.width(16)) comparator_1 (.a(Data_1), .b(Data_2), .eq(Equal), .lt(LE));  // open: gt
  or or_2 (ble_equ_or_les, Equal, LE);
  not not_1 (bne_not_equ, Equal);
  Multiplexer #(.select(3), .width(16)) multiplexer_1 (
    .in0(Data_2), .in1(adder_1_out), .in2(subtractor_1_out), .in3(and_1_out), .in4(or_1_out), .in7(Data_1),
    .out(ALU_OUTPUT), .sel(ALU_Select), .en(1'b1));  // open: in5, in6
  Multiplexer #(.select(3)) multiplexer_2 (
    .in0(1'b0), .in1(1'b0), .in2(1'b0), .in3(1'b0), .in4(1'b0), .in5(ble_equ_or_les), .in6(bne_not_equ),
    .in7(1'b0), .out(ble_bne_out), .sel(ALU_Select), .en(1'b1));

  // Notes on the sheet:
  //   li (Data1)
  //   li(Data2)
  //   ADD
  //   SUB
  //   ADN
  //   OR
  //   COMPARE
endmodule

module Control (
  input  Op0,
  input  Op1,
  input  Op2,
  input  Op3,
  output RegDst,
  output RegWrite,
  output ALUSrc,
  output MemRead,
  output MemWrite,
  output Branch,
  output Jump,
  output MemToReg,
  output ALUOp1,
  output ALUOp2,
  output ALUOp3
);

  wire and_1_out, and_2_out, and_3_out, and_4_out, and_5_out, and_6_out, and_7_out, and_8_out, and_9_out,
       and_13_out, and_14_out, and_15_out, and_16_out, and_18_out, and_19_out, and_20_out, and_21_out,
       and_22_out, not_1_out, not_2_out, not_3_out, not_4_out, not_5_out, not_6_out, not_7_out, not_8_out,
       not_9_out, not_10_out, not_11_out, not_12_out, not_13_out, not_14_out, not_15_out, not_16_out,
       not_17_out, not_18_out, not_19_out, not_20_out, not_21_out, not_22_out, not_23_out, not_24_out,
       not_25_out, not_26_out, not_27_out, not_28_out, not_29_out, not_30_out;

  and and_1 (and_1_out, Op0, Op1, not_1_out);
  not not_1 (not_1_out, Op2);
  and and_2 (and_2_out, Op0, Op1, not_2_out);
  not not_2 (not_2_out, Op3);
  not not_3 (not_3_out, Op0);
  and and_3 (and_3_out, not_3_out, not_4_out);
  not not_4 (not_4_out, Op3);
  not not_5 (not_5_out, Op1);
  and and_4 (and_4_out, not_5_out, not_6_out);
  not not_6 (not_6_out, Op2);
  not not_7 (not_7_out, Op0);
  and and_5 (and_5_out, not_7_out, Op2);
  not not_8 (not_8_out, Op2);
  and and_6 (and_6_out, Op0, not_8_out, Op3);
  not not_9 (not_9_out, Op2);
  and and_7 (and_7_out, not_9_out, not_10_out);
  not not_10 (not_10_out, Op3);
  and and_8 (and_8_out, Op1, Op3);
  and and_9 (and_9_out, Op0, not_11_out);
  not not_11 (not_11_out, Op2);
  not not_12 (not_12_out, Op0);
  not not_13 (not_13_out, Op2);
  not not_14 (not_14_out, Op1);
  and and_10 (Branch, Op0, not_14_out, Op2);
  and and_11 (Jump, Op0, Op1, not_15_out);
  not not_15 (not_15_out, Op2);
  and and_12 (MemToReg, Op1, not_16_out);
  not not_16 (not_16_out, Op2);
  not not_17 (not_17_out, Op1);
  and and_13 (and_13_out, not_17_out, not_18_out, not_19_out);
  not not_18 (not_18_out, Op2);
  not not_19 (not_19_out, Op3);
  not not_20 (not_20_out, Op0);
  and and_14 (and_14_out, not_20_out, not_21_out, Op2);
  not not_21 (not_21_out, Op1);
  not not_22 (not_22_out, Op0);
  and and_15 (and_15_out, not_22_out, Op2, not_23_out);
  not not_23 (not_23_out, Op3);
  not not_24 (not_24_out, Op2);
  and and_16 (and_16_out, Op0, not_24_out, Op3);
  not not_25 (not_25_out, Op0);
  not not_26 (not_26_out, Op1);
  not not_27 (not_27_out, Op2);
  not not_28 (not_28_out, Op3);
  not not_29 (not_29_out, Op1);
  not not_30 (not_30_out, Op3);
  or or_1 (RegDst, and_1_out, and_2_out);
  or or_2 (RegWrite, and_3_out, and_4_out, and_5_out, and_6_out);
  or or_3 (ALUSrc, and_7_out, and_8_out, and_9_out);
  and and_17 (MemWrite, not_12_out, Op1, not_13_out, Op3);
  or or_4 (ALUOp2, and_13_out, and_14_out, and_15_out, and_16_out);
  and and_18 (and_18_out, not_25_out, not_26_out, not_27_out, not_28_out);
  and and_19 (and_19_out, not_29_out, Op2, Op3);
  and and_20 (and_20_out, Op1, Op2, not_30_out);
  and and_21 (and_21_out, Op0, Op3);
  and and_22 (and_22_out, Op0, Op2);
  or or_5 (ALUOp3, and_18_out, and_19_out, and_20_out, and_21_out, and_22_out);

  assign ALUOp1 = 1'b0;
  assign MemRead = 1'b0;
endmodule

module new_Con (
  input  opcode0,
  input  opcode1,
  input  opcode2,
  input  opcode3,
  output RegDst,
  output RegWrite,
  output ALUSrc,
  output ALUOp0,
  output ALUOp1,
  output ALUOp2,
  output MemRead,
  output MemWrite,
  output MemToReg,
  output Branch,
  output Jump,
  output Halt
);

  wire and_1_out, and_2_out, and_3_out, and_4_out, and_5_out, and_6_out, and_7_out, and_8_out, and_9_out,
       and_10_out, and_11_out, and_12_out, and_15_out, and_16_out, and_19_out, and_20_out, and_21_out,
       and_22_out, not_1_out, not_2_out, not_3_out, not_4_out, not_5_out, not_6_out, not_7_out, not_8_out,
       not_9_out, not_10_out, not_11_out, not_12_out, not_13_out, not_14_out, not_15_out, not_16_out,
       not_17_out, not_18_out, not_19_out, not_20_out, not_21_out, not_22_out, not_23_out, not_24_out,
       not_25_out, not_26_out;

  not not_1 (not_1_out, opcode1);
  not not_2 (not_2_out, opcode3);
  and and_1 (and_1_out, not_2_out, not_3_out);
  not not_3 (not_3_out, opcode0);
  not not_4 (not_4_out, opcode2);
  and and_2 (and_2_out, not_4_out, not_5_out);
  not not_5 (not_5_out, opcode1);
  not not_6 (not_6_out, opcode3);
  and and_3 (and_3_out, not_6_out, opcode1);
  and and_4 (and_4_out, opcode3, not_7_out, opcode0);
  not not_7 (not_7_out, opcode1);
  not not_8 (not_8_out, opcode1);
  and and_5 (and_5_out, not_8_out, not_9_out);
  not not_9 (not_9_out, opcode0);
  and and_6 (and_6_out, opcode2, opcode0);
  and and_7 (and_7_out, opcode3, not_10_out);
  not not_10 (not_10_out, opcode1);
  not not_11 (not_11_out, opcode2);
  and and_8 (and_8_out, not_11_out, opcode1);
  and and_9 (and_9_out, opcode3, opcode0);
  and and_10 (and_10_out, opcode3, opcode2);
  not not_12 (not_12_out, opcode2);
  not not_13 (not_13_out, opcode1);
  not not_14 (not_14_out, opcode0);
  not not_15 (not_15_out, opcode3);
  not not_16 (not_16_out, opcode1);
  and and_11 (and_11_out, not_15_out, not_16_out, opcode0);
  and and_12 (and_12_out, opcode3, not_17_out);
  not not_17 (not_17_out, opcode0);
  not not_18 (not_18_out, opcode3);
  not not_19 (not_19_out, opcode1);
  not not_20 (not_20_out, opcode0);
  not not_21 (not_21_out, opcode3);
  not not_22 (not_22_out, opcode1);
  and and_13 (MemToReg, opcode2, not_23_out);
  not not_23 (not_23_out, opcode1);
  not not_24 (not_24_out, opcode2);
  and and_14 (Branch, opcode3, not_24_out, opcode1);
  and and_15 (and_15_out, opcode3, opcode2, not_25_out);
  not not_25 (not_25_out, opcode1);
  and and_16 (and_16_out, opcode3, opcode2, not_26_out);
  not not_26 (not_26_out, opcode0);
  and and_17 (Halt, opcode3, opcode2, opcode1, opcode0);
  and and_18 (RegDst, opcode3, opcode2, not_1_out, opcode0);
  or or_1 (RegWrite, and_1_out, and_2_out, and_3_out, and_4_out);
  or or_2 (ALUSrc, and_5_out, and_6_out, and_7_out);
  or or_3 (ALUOp0, and_8_out, and_9_out, and_10_out);
  and and_19 (and_19_out, opcode3, not_12_out, not_13_out, not_14_out);
  or or_4 (ALUOp1, and_19_out, and_20_out);
  and and_20 (and_20_out, opcode3, opcode1, opcode0);
  or or_5 (ALUOp2, and_11_out, opcode2, and_12_out);
  and and_21 (and_21_out, not_18_out, opcode2, not_19_out, not_20_out);
  or or_6 (MemRead, and_21_out, and_22_out);
  and and_22 (and_22_out, opcode3, opcode2, opcode1, opcode0);
  and and_23 (MemWrite, not_21_out, opcode2, not_22_out, opcode0);
  or or_7 (Jump, and_15_out, and_16_out);
endmodule

module test (
  input  [15:0] in_1,
  input  in_2,
  input  [15:0] in_3,
  input  in_4,
  input  [15:0] in_5,
  input  [15:0] in_6,
  input  in_7,
  input  in_8,
  output [3:0] out_9,
  output [2:0] out_10,
  output [2:0] out_11,
  output Call,
  output rtn
);

  wire not_1_out, not_2_out, undriven, undriven_2, undriven_3, undriven_4;

  Register #(.width(16)) register_1 (.D(in_1), .en(in_2), .clk(in_4));  // open: Q, clr
  and and_1 (Call, undriven, undriven_2, not_1_out, undriven_4);
  not not_1 (not_1_out, undriven_3);
  and and_2 (rtn, undriven, undriven_2, undriven_3, not_2_out);
  not not_2 (not_2_out, undriven_4);
  RAM #(.addrWidth(16), .dataWidth(16), .bus("separate")) ram_1 (
    .addr(in_5), .din(in_6), .str(in_7), .clk(in_8));  // open: data, sel, ld, clr

  assign out_9 = in_3[3:0];
  assign out_10 = in_3[6:4];
  assign out_11 = in_3[9:7];
endmodule

module new_new_Con (
  input  opocode3,
  input  opcode2,
  input  opcode1,
  input  opcode0,
  output RegDst,
  output RegWrite,
  output ALUSrc,
  output ALUOp2,
  output ALUOp1,
  output ALUOp0,
  output MemRead,
  output MemWrite,
  output MemToReg,
  output Branch,
  output Jump,
  output Halt,
  output Call,
  output rtn
);

  wire and_1_out, and_2_out, and_3_out, and_4_out, and_5_out, and_6_out, and_7_out, and_8_out, and_9_out,
       and_10_out, and_11_out, and_12_out, and_13_out, and_14_out, and_16_out, and_17_out, and_19_out,
       and_20_out, and_21_out, and_22_out, and_23_out, and_24_out, and_25_out, and_28_out, and_29_out,
       not_1_out, not_2_out, not_3_out, not_4_out, not_5_out, not_6_out, not_7_out, not_8_out, not_9_out,
       not_10_out, not_11_out, not_12_out, not_13_out, not_14_out, not_15_out, not_16_out, not_17_out,
       not_18_out, not_19_out, not_20_out, not_21_out, not_22_out, not_23_out, not_24_out, not_25_out,
       not_26_out, not_27_out, not_28_out, not_29_out, not_30_out, not_31_out, not_32_out, not_33_out,
       not_34_out, not_35_out, not_36_out, not_37_out, not_38_out, not_39_out, not_40_out, not_41_out;

  not not_1 (not_1_out, opocode3);
  not not_2 (not_2_out, opcode2);
  not not_3 (not_3_out, opocode3);
  not not_4 (not_4_out, opcode2);
  not not_5 (not_5_out, opcode1);
  not not_6 (not_6_out, opocode3);
  and and_1 (and_1_out, not_6_out, not_7_out);
  not not_7 (not_7_out, opcode0);
  not not_8 (not_8_out, opcode2);
  and and_2 (and_2_out, not_8_out, not_9_out);
  not not_9 (not_9_out, opcode1);
  not not_10 (not_10_out, opocode3);
  and and_3 (and_3_out, not_10_out, opcode1);
  not not_11 (not_11_out, opcode1);
  and and_4 (and_4_out, opocode3, not_11_out, opcode0);
  not not_12 (not_12_out, opcode1);
  and and_5 (and_5_out, not_12_out, not_13_out);
  not not_13 (not_13_out, opcode0);
  and and_6 (and_6_out, opcode2, opcode0);
  and and_7 (and_7_out, opocode3, not_14_out);
  not not_14 (not_14_out, opcode1);
  not not_15 (not_15_out, opcode2);
  and and_8 (and_8_out, not_15_out, opcode1, opcode0);
  and and_9 (and_9_out, opcode2, not_16_out, opcode0);
  not not_16 (not_16_out, opcode1);
  and and_10 (and_10_out, opocode3, opcode0);
  and and_11 (and_11_out, opocode3, opcode1);
  not not_17 (not_17_out, opocode3);
  not not_18 (not_18_out, opcode2);
  not not_19 (not_19_out, opcode0);
  not not_20 (not_20_out, opocode3);
  not not_21 (not_21_out, opcode1);
  not not_22 (not_22_out, opcode1);
  not not_23 (not_23_out, opcode0);
  not not_24 (not_24_out, opocode3);
  not not_25 (not_25_out, opcode1);
  and and_12 (and_12_out, not_24_out, not_25_out, opcode0);
  and and_13 (and_13_out, opcode1, not_26_out);
  not not_26 (not_26_out, opcode0);
  and and_14 (and_14_out, opocode3, not_27_out);
  not not_27 (not_27_out, opcode0);
  not not_28 (not_28_out, opocode3);
  not not_29 (not_29_out, opcode1);
  not not_30 (not_30_out, opcode0);
  not not_31 (not_31_out, opocode3);
  not not_32 (not_32_out, opcode1);
  not not_33 (not_33_out, opocode3);
  not not_34 (not_34_out, opcode1);
  not not_35 (not_35_out, opcode0);
  not not_36 (not_36_out, opcode1);
  not not_37 (not_37_out, opcode2);
  and and_15 (Branch, opocode3, not_37_out, opcode1);
  and and_16 (and_16_out, opocode3, opcode2, not_38_out);
  not not_38 (not_38_out, opcode1);
  and and_17 (and_17_out, opocode3, opcode2, not_39_out);
  not not_39 (not_39_out, opcode0);
  and and_18 (Halt, opocode3, opcode2, opcode1, opcode0);
  and and_19 (and_19_out, not_1_out, not_2_out, opcode0);
  and and_20 (and_20_out, not_3_out, not_4_out, opcode1);
  or or_1 (RegDst, and_19_out, and_20_out, and_21_out);
  and and_21 (and_21_out, opocode3, opcode2, not_5_out, opcode0);
  or or_2 (RegWrite, and_1_out, and_2_out, and_3_out, and_4_out);
  or or_3 (ALUSrc, and_5_out, and_6_out, and_7_out);
  or or_4 (ALUOp2, and_8_out, and_9_out, and_10_out, and_11_out);
  and and_22 (and_22_out, not_17_out, not_18_out, opcode1, not_19_out);
  and and_23 (and_23_out, not_20_out, opcode2, not_21_out, opcode0);
  and and_24 (and_24_out, opocode3, not_22_out, not_23_out);
  and and_25 (and_25_out, opocode3, opcode1, opcode0);
  or or_5 (ALUOp0, and_12_out, and_13_out, opcode2, and_14_out);
  and and_26 (MemRead, not_28_out, opcode2, not_29_out, not_30_out);
  and and_27 (MemWrite, not_31_out, opcode2, not_32_out, opcode0);
  and and_28 (and_28_out, not_33_out, opcode2, not_34_out, not_35_out);
  or or_6 (MemToReg, and_28_out, and_29_out);
  and and_29 (and_29_out, opocode3, opcode2, not_36_out, opcode0);
  or or_7 (Jump, and_16_out, and_17_out);
  and and_30 (Call, opocode3, opcode2, not_40_out, opcode0);
  not not_40 (not_40_out, opcode1);
  and and_31 (rtn, opocode3, opcode2, opcode1, not_41_out);
  not not_41 (not_41_out, opcode0);
  or or_8 (ALUOp1, and_22_out, and_23_out, and_24_out, and_25_out);
endmodule
