// Logisim project HW4.circ as structural Verilog: 5 circuits, main circuit main
module main (
  output [15:0] out_1
);

  wire [15:0] PC_q;

  Register #(.width(16)) PC (.en(1'b1), .Q(PC_q));  // open: D, clk, clr
  Adder #(.width(16)) adder_1 (.a(PC_q), .cin(1'b1));  // open: b, out, cout
  ROM #(.addrWidth(16), .dataWidth(16)) rom_1 (.addr(PC_q), .data(out_1));  // open: sel
endmodule

module ALU (
  input  [15:0] Data_1,
  input  [15:0] Data_2,
  input  [2:0] ALU_Select,
  output [15:0] Min,
  output [15:0] Max,
  output bitsignal,
  output [15:0] ALU_OUTPUT
);

  wire comparator_1_gt;
  wire [15:0] adder_1_out, and_1_out, multiplier_1_out, negator_1_out, or_1_out, shifter_1_out,
       shifter_2_out, shifter_3_out;

  assign and_1_out = Data_1 & Data_2;  // AND_Gate and_1, 16 bits wide
  assign or_1_out = Data_1 | Data_2;  // OR_Gate or_1, 16 bits wide
  Multiplexer #(.width(16), .enable("false")) multiplexer_1 (
    .in0(Data_1), .in1(Data_2), .out(Min), .sel(comparator_1_gt));
  Comparator #(.width(16)) comparator_1 (.a(Data_1), .b(Data_2), .gt(comparator_1_gt), .lt(bitsignal));  // open: eq
  Adder #(.width(16)) adder_1 (.a(Data_1), .b(Data_2), .out(adder_1_out));  // open: cin, cout
  Multiplier #(.width(16)) multiplier_1 (.a(Data_1), .b(Data_2), .out(multiplier_1_out));  // open: cin, cout
  Shifter #(.width(16)) shifter_1 (.in(Data_1), .\dist (Data_2[3:0]), .out(shifter_1_out));
  Shifter #(.width(16), .shift("lr")) shifter_2 (.in(Data_2), .\dist (Data_2[3:0]), .out(shifter_2_out));
  Shifter #(.width(16), .shift("ar")) shifter_3 (.in(Data_2), .\dist (Data_2[3:0]), .out(shifter_3_out));
  Negator #(.width(16)) negator_1 (.in(Data_1), .out(negator_1_out));
  Multiplexer #(.width(16), .enable("false")) multiplexer_2 (.in0(Data_1), .in1(Data_2), .out(Max), .sel(bitsignal));
  Multiplexer #(.select(3), .width(16)) multiplexer_3 (
    .in0(adder_1_out), .in1(and_1_out), .in2(or_1_out), .in3(multiplier_1_out), .in4(shifter_1_out),
    .in5(shifter_2_out), .in6(shifter_3_out), .in7(negator_1_out), .out(ALU_OUTPUT), .sel(ALU_Select),
    .en(1'b1));

  // Notes on the sheet:
  //   Lshift
  //   Rshift
  //   ARshift
  //   Neg
  //   or
  //   Mul
  //   add
  //   and
endmodule

module ALU_Control1 (
  input  ALU_OP1,
  input  ALU_OP2,
  input  ALU_OP3,
  input  ALU_OP4,
  output [3:0] out_5,
  output [3:0] ALU_Control
);

  wire [3:0] adder_1_out, adder_2_out, bit_extender_2_out, bit_extender_3_out, bit_extender_4_out,
       shifter_1_out, shifter_2_out, shifter_3_out;

  assign out_5 = {{3{1'b0}}, ALU_OP1};  // Bit_Extender bit_extender_1
  assign bit_extender_2_out = {{3{1'b0}}, ALU_OP2};  // Bit_Extender bit_extender_2
  assign bit_extender_3_out = {{3{1'b0}}, ALU_OP3};  // Bit_Extender bit_extender_3
  Shifter #(.width(4)) shifter_1 (.in(out_5), .\dist (2'b11), .out(shifter_1_out));
  Shifter #(.width(4)) shifter_2 (.in(bit_extender_2_out), .\dist (2'b10), .out(shifter_2_out));
  Shifter #(.width(4)) shifter_3 (.in(bit_extender_3_out), .\dist (2'b01), .out(shifter_3_out));
  assign bit_extender_4_out = {{3{1'b0}}, ALU_OP4};  // Bit_Extender bit_extender_4
  Adder #(.width(4)) adder_1 (.a(shifter_1_out), .b(shifter_2_out), .out(adder_1_out));  // open: cin, cout
  Adder #(.width(4)) adder_2 (.a(shifter_3_out), .b(bit_extender_4_out), .out(adder_2_out));  // open: cin, cout
  Adder #(.width(4)) adder_3 (.a(adder_1_out), .b(adder_2_out), .out(ALU_Control));  // open: cin, cout
endmodule

module Register_File (
  input  write_enable,
  input  [2:0] read_reg1,
  input  [2:0] read_reg2,
  input  [2:0] write_reg_position,
  input  [15:0] data_Input,
  input  clock,
  input  reset,
  output [15:0] data_1,
  output [15:0] data_2
);

  wire and_1_out, and_2_out, and_3_out, and_4_out, and_5_out, and_6_out, and_7_out, and_8_out,
       decoder_1_out0, decoder_1_out1, decoder_1_out2, decoder_1_out3, decoder_1_out4, decoder_1_out5,
       decoder_1_out6, decoder_1_out7;
  wire [15:0] register_1_q, register_2_q, register_3_q, register_4_q, register_5_q, register_6_q,
       register_7_q, register_8_q;

  Decoder #(.select(3), .enable("false")) decoder_1 (
    .out0(decoder_1_out0), .out1(decoder_1_out1), .out2(decoder_1_out2), .out3(decoder_1_out3),
    .out4(decoder_1_out4), .out5(decoder_1_out5), .out6(decoder_1_out6), .out7(decoder_1_out7),
    .sel(write_reg_position));
  and and_1 (and_1_out, decoder_1_out0, write_enable);
  and and_2 (and_2_out, decoder_1_out1, write_enable);
  and and_3 (and_3_out, decoder_1_out2, write_enable);
  and and_4 (and_4_out, decoder_1_out3, write_enable);
  and and_5 (and_5_out, decoder_1_out4, write_enable);
  and and_6 (and_6_out, decoder_1_out5, write_enable);
  and and_7 (and_7_out, decoder_1_out6, write_enable);
  and and_8 (and_8_out, decoder_1_out7, write_enable);
  Register #(.width(16)) register_1 (.D(data_Input), .en(and_1_out), .Q(register_1_q), .clk(clock), .clr(reset));
  Register #(.width(16)) register_2 (.D(data_Input), .en(and_2_out), .Q(register_2_q), .clk(clock), .clr(reset));
  Register #(.width(16)) register_3 (.D(data_Input), .en(and_3_out), .Q(register_3_q), .clk(clock), .clr(reset));
  Register #(.width(16)) register_4 (.D(data_Input), .en(and_4_out), .Q(register_4_q), .clk(clock), .clr(reset));
  Register #(.width(16)) register_5 (.D(data_Input), .en(and_5_out), .Q(register_5_q), .clk(clock), .clr(reset));
  Register #(.width(16)) register_6 (.D(data_Input), .en(and_6_out), .Q(register_6_q), .clk(clock), .clr(reset));
  Register #(.width(16)) register_7 (.D(data_Input), .en(and_7_out), .Q(register_7_q), .clk(clock), .clr(reset));
  Register #(.width(16)) register_8 (.D(data_Input), .en(and_8_out), .Q(register_8_q), .clk(clock), .clr(reset));
  Multiplexer #(.select(3), .width(16), .enable("false")) multiplexer_1 (
    .in0(register_1_q), .in1(register_2_q), .in2(register_3_q), .in3(register_4_q), .in4(register_5_q),
    .in5(register_6_q), .in6(register_7_q), .in7(register_8_q), .out(data_1), .sel(read_reg1));
  Multiplexer #(.select(3), .width(16), .enable("false")) multiplexer_2 (
    .in0(register_1_q), .in1(register_2_q), .in2(register_3_q), .in3(register_4_q), .in4(register_5_q),
    .in5(register_6_q), .in6(register_7_q), .in7(register_8_q), .out(data_2), .sel(read_reg2));
endmodule

module ALU_Control2 (
  input  ALU_OP1,
  input  ALU_OP2,
  input  ALU_OP3,
  input  ALU_OP4,
  output Jump,
  output Call,
  output RTN,
  output REBOOT
);

  wire not_1_out, not_2_out, not_3_out, not_4_out, not_5_out;

  not not_1 (not_1_out, ALU_OP2);
  not not_2 (not_2_out, ALU_OP2);
  not not_3 (not_3_out, ALU_OP3);
  not not_4 (not_4_out, ALU_OP4);
  not not_5 (not_5_out, ALU_OP3);
  and and_1 (Jump, ALU_OP1, not_1_out, ALU_OP3);
  and and_2 (Call, ALU_OP1, not_2_out, ALU_OP3, ALU_OP4);
  and and_3 (RTN, ALU_OP1, ALU_OP2, not_3_out, not_4_out);
  and and_4 (REBOOT, ALU_OP1, ALU_OP2, not_5_out, ALU_OP4);
endmodule
